// Logisim project alu.circ as structural Verilog: 8 circuits, main circuit alu
module alu (
  input  [31:0] A,
  input  [31:0] B,
  input  [3:0] ALUSel,
  output [31:0] Result
);

  wire comparator_1_lt;
  wire [31:0] add0, and1, mul10, mulh14, mulhu11, or2, sll6, slt7, sra5, srl4, sub12, xor3;

  Adder #(.width(32)) adder_1 (.a(A), .b(B), .out(add0));  // open: cin, cout
  assign and1 = A & B;  // AND_Gate and_1, 32 bits wide
  assign or2 = A | B;  // OR_Gate or_1, 32 bits wide
  assign xor3 = A ^ B;  // XOR_Gate xor_1, 32 bits wide
  Comparator #(.width(32)) comparator_1 (.a(A), .b(B), .lt(comparator_1_lt));  // open: gt, eq
  Multiplier #(.width(32)) multiplier_1 (.a(A), .b(B), .cout(mulhu11));  // open: out, cin
  Subtractor #(.width(32)) subtractor_1 (.a(A), .b(B), .out(sub12));  // open: bin, bout
  assign slt7 = {{31{1'b0}}, comparator_1_lt};  // Bit_Extender bit_extender_1
  srl32 srl32_1 (.in_1(A), .in_2(B), .out_3(srl4));
  sra32 sra32_1 (.in_1(A), .in_2(B), .out_3(sra5));
  sll32 sll32_1 (.in_1(A), .in_2(B), .out_3(sll6));
  mul32 mul32_1 (.input0(A), .input1(B), .ouput0(mul10));
  mulh32 mulh32_1 (.input0(A), .input1(B), .output0(mulh14));
  Multiplexer #(.enable("false"), .select(4), .width(32)) multiplexer_1 (
    .in0(add0), .in1(and1), .in2(or2), .in3(xor3), .in4(srl4), .in5(sra5), .in6(sll6), .in7(slt7),
    .in10(mul10), .in11(mulhu11), .in12(sub12), .in13(B), .in14(mulh14), .out(Result), .sel(ALUSel));  // open: in8, in9, in15

  // Other names for the same wires on the sheet: bsel13[31:0] = B

  // Notes on the sheet:
  //   INPUTS to your circuit
  //   DON'T CHANGE THE LOCATIONS OF THE INPUTS AND OUTPUTS!
  //   OUTPUT from your circuit
endmodule

module srl32 (
  input  [31:0] in_1,
  input  [31:0] in_2,
  output [31:0] out_3
);

  wire [4:0] bit_extender_1_out;

  Bit_Extender #(.in_width(32), .out_width(5), .\type ("zero")) bit_extender_1 (.in(in_2), .out(bit_extender_1_out));
  Shifter #(.shift("lr"), .width(32)) shifter_1 (.in(in_1), .\dist (bit_extender_1_out), .out(out_3));
endmodule

module sra32 (
  input  [31:0] in_1,
  input  [31:0] in_2,
  output [31:0] out_3
);

  wire [4:0] bit_extender_1_out;

  Bit_Extender #(.in_width(32), .out_width(5), .\type ("zero")) bit_extender_1 (.in(in_2), .out(bit_extender_1_out));
  Shifter #(.shift("ar"), .width(32)) shifter_1 (.in(in_1), .\dist (bit_extender_1_out), .out(out_3));
endmodule

module sll32 (
  input  [31:0] in_1,
  input  [31:0] in_2,
  output [31:0] out_3
);

  wire [4:0] bit_extender_1_out;

  Bit_Extender #(.in_width(32), .out_width(5), .\type ("zero")) bit_extender_1 (.in(in_2), .out(bit_extender_1_out));
  Shifter #(.width(32)) shifter_1 (.in(in_1), .\dist (bit_extender_1_out), .out(out_3));
endmodule

module mul32 (
  input  [31:0] input0,
  input  [31:0] input1,
  output [31:0] ouput0
);

  wire convert_to_positive_number_1_output_sign, convert_to_positive_number_2_output_sign, xor_1_out;
  wire [31:0] convert_to_positive_number_1_output_num, convert_to_positive_number_2_output_num,
       multiplier_1_cout, multiplier_1_out;
  wire [63:0] negator_1_out;

  // Probe on input0
  // Probe on input1
  convert_to_positive_number convert_to_positive_number_1 (
    .Input0(input0), .output_num(convert_to_positive_number_1_output_num),
    .output_sign(convert_to_positive_number_1_output_sign));
  convert_to_positive_number convert_to_positive_number_2 (
    .Input0(input1), .output_num(convert_to_positive_number_2_output_num),
    .output_sign(convert_to_positive_number_2_output_sign));
  xor xor_1 (xor_1_out, convert_to_positive_number_1_output_sign, convert_to_positive_number_2_output_sign);
  Multiplier #(.width(32)) multiplier_1 (
    .a(convert_to_positive_number_1_output_num), .b(convert_to_positive_number_2_output_num),
    .out(multiplier_1_out), .cout(multiplier_1_cout));  // open: cin
  Negator #(.width(64)) negator_1 (.in({multiplier_1_cout, multiplier_1_out}), .out(negator_1_out));
  // Probe on ouput0
  Multiplexer #(.enable("false"), .width(32)) multiplexer_1 (
    .in0(multiplier_1_out), .in1(negator_1_out[31:0]), .out(ouput0), .sel(xor_1_out));
endmodule

module convert_to_positive_number (
  input  [31:0] Input0,
  output [31:0] output_num,
  output output_sign
);

  wire [31:0] not_1_out, subtractor_1_out;

  Subtractor #(.width(32)) subtractor_1 (.a(Input0), .b(32'h1), .out(subtractor_1_out));  // open: bin, bout
  assign not_1_out = ~subtractor_1_out;  // NOT_Gate not_1, 32 bits wide
  Multiplexer #(.enable("false"), .width(32)) multiplexer_1 (
    .in0(Input0), .in1(not_1_out), .out(output_num), .sel(Input0[31]));

  assign output_sign = Input0[31];
endmodule

module convert_to_positive_number64 (
  input  [63:0] Input0,
  output [63:0] output_num,
  output output_sign
);

  wire [63:0] adder_1_out, not_1_out;

  BitSelector #(.width(64)) bitselector_1 (.in(Input0), .out(output_sign), .sel({6{1'b1}}));
  assign not_1_out = ~adder_1_out;  // NOT_Gate not_1, 64 bits wide
  Adder #(.width(64)) adder_1 (.a({64{1'b1}}), .b(Input0), .out(adder_1_out));  // open: cin, cout
  Multiplexer #(.enable("false"), .width(64)) multiplexer_1 (
    .in0(Input0), .in1(not_1_out), .out(output_num), .sel(output_sign));
endmodule

module mulh32 (
  input  [31:0] input0,
  input  [31:0] input1,
  output [31:0] output0
);

  wire convert_to_positive_number64_1_output_sign, convert_to_positive_number64_2_output_sign,
       convert_to_positive_number_1_output_sign, convert_to_positive_number_2_output_sign, xor_1_out,
       xor_2_out;
  wire [31:0] convert_to_positive_number_1_output_num, convert_to_positive_number_2_output_num,
       multiplier_2_cout, multiplier_2_out, negator_2_out, negator_2_out_2;
  wire [63:0] convert_to_positive_number64_1_output_num, convert_to_positive_number64_2_output_num,
       multiplexer_1_out, multiplier_1_cout, multiplier_1_out, negator_1_out;

  // Probe on {input0, {32{1'b0}}}
  // Probe on {input1, {32{1'b0}}}
  convert_to_positive_number64 convert_to_positive_number64_1 (
    .Input0({input0, {32{1'b0}}}), .output_num(convert_to_positive_number64_1_output_num),
    .output_sign(convert_to_positive_number64_1_output_sign));
  convert_to_positive_number64 convert_to_positive_number64_2 (
    .Input0({input1, {32{1'b0}}}), .output_num(convert_to_positive_number64_2_output_num),
    .output_sign(convert_to_positive_number64_2_output_sign));
  // Probe on multiplier_1_cout
  convert_to_positive_number convert_to_positive_number_1 (
    .Input0(input0), .output_num(convert_to_positive_number_1_output_num),
    .output_sign(convert_to_positive_number_1_output_sign));
  convert_to_positive_number convert_to_positive_number_2 (
    .Input0(input1), .output_num(convert_to_positive_number_2_output_num),
    .output_sign(convert_to_positive_number_2_output_sign));
  // Probe on multiplier_1_out
  Multiplier #(.width(64)) multiplier_1 (
    .a(convert_to_positive_number64_1_output_num), .b(convert_to_positive_number64_2_output_num),
    .out(multiplier_1_out), .cout(multiplier_1_cout));  // open: cin
  xor xor_1 (xor_1_out, convert_to_positive_number64_1_output_sign, convert_to_positive_number64_2_output_sign);
  xor xor_2 (xor_2_out, convert_to_positive_number_1_output_sign, convert_to_positive_number_2_output_sign);
  Negator #(.width(64)) negator_1 (.in(multiplier_1_cout), .out(negator_1_out));
  // Probe on multiplier_2_out
  Multiplier #(.width(32)) multiplier_2 (
    .a(convert_to_positive_number_1_output_num), .b(convert_to_positive_number_2_output_num),
    .out(multiplier_2_out), .cout(multiplier_2_cout));  // open: cin
  // Probe on multiplier_2_cout
  Multiplexer #(.enable("false"), .width(64)) multiplexer_1 (
    .in0(multiplier_1_cout), .in1(negator_1_out), .out(multiplexer_1_out), .sel(xor_1_out));
  // Probe on multiplexer_1_out[63:32]
  Negator #(.width(64)) negator_2 (.in({multiplier_2_cout, multiplier_2_out}), .out({negator_2_out_2, negator_2_out}));
  Multiplexer #(.enable("false"), .width(32)) multiplexer_2 (
    .in0(multiplier_2_cout), .in1(negator_2_out_2), .out(output0), .sel(xor_2_out));

  // Notes on the sheet:
  //   这是一个反例，最开始考虑实现64位的乘法，然后再将最高有效位取出，电路运行结果虽然正确，但是多了很多不必要的计算，因为这种方式实现的"低64位"都是0。排查过程发现mul32其实自己一开始搞错了，模拟器内部的乘法运算器输出的结果保存在两个位置Output和Carryout上，在根据符号位重新计算product时候，需要将两个输出结果合并成一个二进制表示的整数(64bit)然后进行 * -1的计算。这是错误的原因。
endmodule
