// Logisim project cpu.circ as structural Verilog: 1 circuit, main circuit cpu
module cpu (
  input  clk,
  input  [31:0] INSTRUCTION,
  input  [31:0] READ_DATA,
  output [31:0] WRITE_ADDRESS,
  output [31:0] PROGRAM_COUNTER,
  output [31:0] ra,
  output [31:0] sp,
  output [31:0] t0,
  output [31:0] t1,
  output [31:0] t2,
  output [31:0] s0,
  output [31:0] s1,
  output [31:0] a0,
  output [31:0] tohost,
  output [3:0] WRITE_ENABLE,
  output [31:0] WRITE_DATA
);

  wire control_logic_1_p2, control_logic_1_p3, control_logic_1_p5, control_logic_1_p6, control_logic_1_p7,
       control_logic_1_p8, control_logic_1_p9, csr_1_p2;
  wire [1:0] control_logic_1_p12;
  wire [2:0] control_logic_1_p4;
  wire [3:0] control_logic_1_p10;
  wire [4:0] rd, rs1, rs2;
  wire [31:0] imm_gen_1_imm, multiplexer_1_out, multiplexer_2_out, multiplexer_3_out, PC_q,
       regfile_1_read_data_1, register_1_q;

  Register #(.width(32)) PC (.D(PROGRAM_COUNTER), .clk(clk), .Q(PC_q));  // open: en, clr
  Register #(.width(32)) register_1 (
    .D(INSTRUCTION), .clk(clk),
    .Q({register_1_q[31:25], rs2, rs1, register_1_q[14:12], rd, register_1_q[6:0]}));  // open: en, clr
  Adder #(.width(32)) adder_1 (.a(32'h4), .b(PC_q), .out(PROGRAM_COUNTER));  // open: cin, cout
  imm_gen imm_gen_1 (
    .inst({register_1_q[31:25], rs2, rs1, register_1_q[14:12], rd, register_1_q[6:0]}),
    .ImmSel(control_logic_1_p4), .imm(imm_gen_1_imm));
  // control_logic control_logic_1: pin names not known; wires that end beside it: {register_1_q[31:25], rs2, rs1, register_1_q[14:12], rd, register_1_q[6:0]}, control_logic_1_p2, control_logic_1_p3, control_logic_1_p4, control_logic_1_p5, control_logic_1_p6, control_logic_1_p7, control_logic_1_p8, control_logic_1_p9, control_logic_1_p10, WRITE_ENABLE, control_logic_1_p12
  regfile regfile_1 (
    .rs1(rs1), .rs2(rs2), .rd(rd), .Write_data(multiplexer_3_out), .RegWEn(control_logic_1_p3), .clk(clk),
    .ra(ra), .sp(sp), .t0(t0), .t1(t1), .t2(t2), .s0(s0), .s1(s1), .a0(a0),
    .Read_Data_1(regfile_1_read_data_1), .Read_Data_2(WRITE_DATA));
  // branch_comp branch_comp_1: pin names not known; wires that end beside it: regfile_1_read_data_1, WRITE_DATA, control_logic_1_p7, control_logic_1_p5, control_logic_1_p6
  Multiplexer #(.enable("false"), .width(32)) multiplexer_1 (
    .in0(regfile_1_read_data_1), .in1(PC_q), .out(multiplexer_1_out), .sel(control_logic_1_p8));
  Multiplexer #(.enable("false"), .width(32)) multiplexer_2 (
    .in0(WRITE_DATA), .in1(imm_gen_1_imm), .out(multiplexer_2_out), .sel(control_logic_1_p9));
  alu alu_1 (.Result(WRITE_ADDRESS), .A(multiplexer_1_out), .B(multiplexer_2_out), .ALUSel(control_logic_1_p10));
  // csr csr_1: pin names not known; wires that end beside it: tohost, csr_1_p2
  Multiplexer #(.enable("false"), .select(2), .width(32)) multiplexer_3 (
    .in0(READ_DATA), .in1(WRITE_ADDRESS), .in2(PROGRAM_COUNTER), .out(multiplexer_3_out),
    .sel(control_logic_1_p12));  // open: in3

  // Notes on the sheet:
  //   Output to IMEM
  //   IMEM (do **NOT** move this)
  //   Inputs from IMEM
  //   Inputs/Outputs for testing. Do **NOT** move these.
  //   Outputs To DMEM
  //   DMEM (do **NOT** move this)
  //   Inputs From DMEM
endmodule
