// Logisim project regfile.circ as structural Verilog: 3 circuits, main circuit regfile
module regfile (
  input  [4:0] rs1,
  input  [4:0] rs2,
  input  [4:0] rd,
  input  [31:0] Write_data,
  input  RegWEn,
  input  clk,
  output [31:0] ra,
  output [31:0] sp,
  output [31:0] t0,
  output [31:0] t1,
  output [31:0] t2,
  output [31:0] s0,
  output [31:0] s1,
  output [31:0] a0,
  output [31:0] Read_Data_1,
  output [31:0] Read_Data_2
);

  wire [31:0] write_register_1_otu_x12, write_register_1_out_x0, write_register_1_out_x3,
       write_register_1_out_x4, write_register_1_out_x11, write_register_1_out_x13, write_register_1_out_x14,
       write_register_1_out_x15, write_register_1_out_x16, write_register_1_out_x17,
       write_register_1_out_x18, write_register_1_out_x19, write_register_1_out_x20,
       write_register_1_out_x21, write_register_1_out_x22, write_register_1_out_x23,
       write_register_1_out_x24, write_register_1_out_x25, write_register_1_out_x26,
       write_register_1_out_x27, write_register_1_out_x28, write_register_1_out_x29,
       write_register_1_out_x30, write_register_1_out_x31;

  write_register write_register_1 (
    .input0_data(Write_data), .input1_wen(RegWEn), .input2_reg_num(rd), .clk(clk),
    .out_x0(write_register_1_out_x0), .out_x1(ra), .out_x2(sp), .out_x3(write_register_1_out_x3),
    .out_x4(write_register_1_out_x4), .out_x5(t0), .out_x6(t1), .out_x7(t2), .out_x8(s0), .out_x9(s1),
    .out_x10(a0), .out_x11(write_register_1_out_x11), .otu_x12(write_register_1_otu_x12),
    .out_x13(write_register_1_out_x13), .out_x14(write_register_1_out_x14),
    .out_x15(write_register_1_out_x15), .out_x16(write_register_1_out_x16),
    .out_x17(write_register_1_out_x17), .out_x18(write_register_1_out_x18),
    .out_x19(write_register_1_out_x19), .out_x20(write_register_1_out_x20),
    .out_x21(write_register_1_out_x21), .out_x22(write_register_1_out_x22),
    .out_x23(write_register_1_out_x23), .out_x24(write_register_1_out_x24),
    .out_x25(write_register_1_out_x25), .out_x26(write_register_1_out_x26),
    .out_x27(write_register_1_out_x27), .out_x28(write_register_1_out_x28),
    .out_x29(write_register_1_out_x29), .out_x30(write_register_1_out_x30), .out_x31(write_register_1_out_x31));
  Multiplexer #(.enable("false"), .select(5), .width(32)) multiplexer_1 (
    .in0(write_register_1_out_x0), .in1(ra), .in2(sp), .in3(write_register_1_out_x3),
    .in4(write_register_1_out_x4), .in5(t0), .in6(t1), .in7(t2), .in8(s0), .in9(s1), .in10(a0),
    .in11(write_register_1_out_x11), .in12(write_register_1_otu_x12), .in13(write_register_1_out_x13),
    .in14(write_register_1_out_x14), .in15(write_register_1_out_x15), .in16(write_register_1_out_x16),
    .in17(write_register_1_out_x17), .in18(write_register_1_out_x18), .in19(write_register_1_out_x19),
    .in20(write_register_1_out_x20), .in21(write_register_1_out_x21), .in22(write_register_1_out_x22),
    .in23(write_register_1_out_x23), .in24(write_register_1_out_x24), .in25(write_register_1_out_x25),
    .in26(write_register_1_out_x26), .in27(write_register_1_out_x27), .in28(write_register_1_out_x28),
    .in29(write_register_1_out_x29), .in30(write_register_1_out_x30), .in31(write_register_1_out_x31),
    .out(Read_Data_1), .sel(rs1));
  Multiplexer #(.enable("false"), .select(5), .width(32)) multiplexer_2 (
    .in0(write_register_1_out_x0), .in1(ra), .in2(sp), .in3(write_register_1_out_x3),
    .in4(write_register_1_out_x4), .in5(t0), .in6(t1), .in7(t2), .in8(s0), .in9(s1), .in10(a0),
    .in11(write_register_1_out_x11), .in12(write_register_1_otu_x12), .in13(write_register_1_out_x13),
    .in14(write_register_1_out_x14), .in15(write_register_1_out_x15), .in16(write_register_1_out_x16),
    .in17(write_register_1_out_x17), .in18(write_register_1_out_x18), .in19(write_register_1_out_x19),
    .in20(write_register_1_out_x20), .in21(write_register_1_out_x21), .in22(write_register_1_out_x22),
    .in23(write_register_1_out_x23), .in24(write_register_1_out_x24), .in25(write_register_1_out_x25),
    .in26(write_register_1_out_x26), .in27(write_register_1_out_x27), .in28(write_register_1_out_x28),
    .in29(write_register_1_out_x29), .in30(write_register_1_out_x30), .in31(write_register_1_out_x31),
    .out(Read_Data_2), .sel(rs2));

  // Other names for the same wires on the sheet: read_data1[31:0] = Read_Data_1; read_data2[31:0] = Read_Data_2;
  //   read_reg1[4:0] = rs1; read_reg2[4:0] = rs2; write_en = RegWEn; write_reg[4:0] = rd

  // Notes on the sheet:
  //   INPUTS to your circuit
  //   DON'T CHANGE THE LOCATIONS OF THE INPUTS AND OUTPUTS!
  //   These are DEBUG/TEST outputs from your circuit.
  //   OUTPUTS from your circuit
endmodule

module write_register (
  input  [31:0] input0_data,
  input  input1_wen,
  input  [4:0] input2_reg_num,
  input  clk,
  output [31:0] out_x0,
  output [31:0] out_x1,
  output [31:0] out_x2,
  output [31:0] out_x3,
  output [31:0] out_x4,
  output [31:0] out_x5,
  output [31:0] out_x6,
  output [31:0] out_x7,
  output [31:0] out_x8,
  output [31:0] out_x9,
  output [31:0] out_x10,
  output [31:0] out_x11,
  output [31:0] otu_x12,
  output [31:0] out_x13,
  output [31:0] out_x14,
  output [31:0] out_x15,
  output [31:0] out_x16,
  output [31:0] out_x17,
  output [31:0] out_x18,
  output [31:0] out_x19,
  output [31:0] out_x20,
  output [31:0] out_x21,
  output [31:0] out_x22,
  output [31:0] out_x23,
  output [31:0] out_x24,
  output [31:0] out_x25,
  output [31:0] out_x26,
  output [31:0] out_x27,
  output [31:0] out_x28,
  output [31:0] out_x29,
  output [31:0] out_x30,
  output [31:0] out_x31
);

  numbered_register x1 (
    .data(input0_data), .reg_number(5'b00001), .sel_number(input2_reg_num), .wen(input1_wen), .clk(clk),
    .output0(out_x1));
  numbered_register x2 (
    .data(input0_data), .reg_number(5'b00010), .sel_number(input2_reg_num), .wen(input1_wen), .clk(clk),
    .output0(out_x2));
  numbered_register x3 (
    .data(input0_data), .reg_number(5'b00011), .sel_number(input2_reg_num), .wen(input1_wen), .clk(clk),
    .output0(out_x3));
  numbered_register x4 (
    .data(input0_data), .reg_number(5'b00100), .sel_number(input2_reg_num), .wen(input1_wen), .clk(clk),
    .output0(out_x4));
  numbered_register x5 (
    .data(input0_data), .reg_number(5'b00101), .sel_number(input2_reg_num), .wen(input1_wen), .clk(clk),
    .output0(out_x5));
  numbered_register x6 (
    .data(input0_data), .reg_number(5'b00110), .sel_number(input2_reg_num), .wen(input1_wen), .clk(clk),
    .output0(out_x6));
  numbered_register x7 (
    .data(input0_data), .reg_number(5'b00111), .sel_number(input2_reg_num), .wen(input1_wen), .clk(clk),
    .output0(out_x7));
  numbered_register x8 (
    .data(input0_data), .reg_number(5'b01000), .sel_number(input2_reg_num), .wen(input1_wen), .clk(clk),
    .output0(out_x8));
  numbered_register x9 (
    .data(input0_data), .reg_number(5'b01001), .sel_number(input2_reg_num), .wen(input1_wen), .clk(clk),
    .output0(out_x9));
  numbered_register x10 (
    .data(input0_data), .reg_number(5'b01010), .sel_number(input2_reg_num), .wen(input1_wen), .clk(clk),
    .output0(out_x10));
  numbered_register x11 (
    .data(input0_data), .reg_number(5'b01011), .sel_number(input2_reg_num), .wen(input1_wen), .clk(clk),
    .output0(out_x11));
  numbered_register x12 (
    .data(input0_data), .reg_number(5'b01100), .sel_number(input2_reg_num), .wen(input1_wen), .clk(clk),
    .output0(otu_x12));
  numbered_register x13 (
    .data(input0_data), .reg_number(5'b01101), .sel_number(input2_reg_num), .wen(input1_wen), .clk(clk),
    .output0(out_x13));
  numbered_register x14 (
    .data(input0_data), .reg_number(5'b01110), .sel_number(input2_reg_num), .wen(input1_wen), .clk(clk),
    .output0(out_x14));
  numbered_register x15 (
    .data(input0_data), .reg_number(5'b01111), .sel_number(input2_reg_num), .wen(input1_wen), .clk(clk),
    .output0(out_x15));
  numbered_register x16 (
    .data(input0_data), .reg_number(5'b10000), .sel_number(input2_reg_num), .wen(input1_wen), .clk(clk),
    .output0(out_x16));
  numbered_register x17 (
    .data(input0_data), .reg_number(5'b10001), .sel_number(input2_reg_num), .wen(input1_wen), .clk(clk),
    .output0(out_x17));
  numbered_register x18 (
    .data(input0_data), .reg_number(5'b10010), .sel_number(input2_reg_num), .wen(input1_wen), .clk(clk),
    .output0(out_x18));
  numbered_register x19 (
    .data(input0_data), .reg_number(5'b10011), .sel_number(input2_reg_num), .wen(input1_wen), .clk(clk),
    .output0(out_x19));
  numbered_register x20 (
    .data(input0_data), .reg_number(5'b10100), .sel_number(input2_reg_num), .wen(input1_wen), .clk(clk),
    .output0(out_x20));
  numbered_register x21 (
    .data(input0_data), .reg_number(5'b10101), .sel_number(input2_reg_num), .wen(input1_wen), .clk(clk),
    .output0(out_x21));
  numbered_register x22 (
    .data(input0_data), .reg_number(5'b10110), .sel_number(input2_reg_num), .wen(input1_wen), .clk(clk),
    .output0(out_x22));
  numbered_register x23 (
    .data(input0_data), .reg_number(5'b10111), .sel_number(input2_reg_num), .wen(input1_wen), .clk(clk),
    .output0(out_x23));
  numbered_register x24 (
    .data(input0_data), .reg_number(5'b11000), .sel_number(input2_reg_num), .wen(input1_wen), .clk(clk),
    .output0(out_x24));
  numbered_register x25 (
    .data(input0_data), .reg_number(5'b11001), .sel_number(input2_reg_num), .wen(input1_wen), .clk(clk),
    .output0(out_x25));
  numbered_register x26 (
    .data(input0_data), .reg_number(5'b11010), .sel_number(input2_reg_num), .wen(input1_wen), .clk(clk),
    .output0(out_x26));
  numbered_register x27 (
    .data(input0_data), .reg_number(5'b11011), .sel_number(input2_reg_num), .wen(input1_wen), .clk(clk),
    .output0(out_x27));
  numbered_register x28 (
    .data(input0_data), .reg_number(5'b11100), .sel_number(input2_reg_num), .wen(input1_wen), .clk(clk),
    .output0(out_x28));
  numbered_register x29 (
    .data(input0_data), .reg_number(5'b11101), .sel_number(input2_reg_num), .wen(input1_wen), .clk(clk),
    .output0(out_x29));
  numbered_register x30 (
    .data(input0_data), .reg_number(5'b11110), .sel_number(input2_reg_num), .wen(input1_wen), .clk(clk),
    .output0(out_x30));
  numbered_register x31 (
    .data(input0_data), .reg_number({5{1'b1}}), .sel_number(input2_reg_num), .wen(input1_wen), .clk(clk),
    .output0(out_x31));

  assign out_x0 = {32{1'b0}};

  // Other names for the same wires on the sheet: input_data[31:0] = input0_data; out_x12[31:0] = otu_x12;
  //   sel_reg[4:0] = input2_reg_num; wen = input1_wen
endmodule

module numbered_register (
  input  [31:0] data,
  input  [4:0] reg_number,
  input  [4:0] sel_number,
  input  wen,
  input  clk,
  output [31:0] output0
);

  wire and_1_out, and_2_out, and_3_out, and_4_out, and_5_out, not_1_out, not_2_out, not_3_out, not_4_out,
       not_5_out, xor_1_out, xor_2_out, xor_3_out, xor_4_out, xor_5_out;

  xor xor_1 (xor_1_out, reg_number[0], sel_number[0]);
  xor xor_2 (xor_2_out, reg_number[1], sel_number[1]);
  xor xor_3 (xor_3_out, reg_number[2], sel_number[2]);
  xor xor_4 (xor_4_out, reg_number[3], sel_number[3]);
  xor xor_5 (xor_5_out, reg_number[4], sel_number[4]);
  not not_1 (not_1_out, xor_1_out);
  not not_2 (not_2_out, xor_2_out);
  not not_3 (not_3_out, xor_3_out);
  not not_4 (not_4_out, xor_4_out);
  not not_5 (not_5_out, xor_5_out);
  and and_1 (and_1_out, not_1_out, not_2_out);
  and and_2 (and_2_out, and_1_out, and_3_out);
  and and_3 (and_3_out, not_3_out, not_4_out);
  and and_4 (and_4_out, and_2_out, not_5_out);
  Register #(.width(32)) register_1 (.D(data), .en(and_5_out), .clk(clk), .Q(output0));  // open: clr
  and and_5 (and_5_out, and_4_out, wen);
endmodule
