// Logisim project multiplication.circ as structural Verilog: 3 circuits, main circuit fsm_logic
module main (
  input  [3:0] input_multiplier,
  input  [3:0] input_mutiplicand,
  input  reset,
  output [7:0] out_4
);

  wire bit_extender_5_out, clock_1_out, clock_2_out, clock_3_out;
  wire [3:0] bit_extender_4_out, register_1_q, shifter_1_out;
  wire [7:0] adder_1_out, bit_extender_1_out, bit_extender_2_out, bit_extender_3_out, fsm_1_output0,
       fsm_2_output0, multiplexer_1_out, multiplicand_q, shifter_2_out;

  assign bit_extender_1_out = {{4{1'b0}}, shifter_1_out};  // Bit_Extender bit_extender_1
  assign bit_extender_2_out = {{4{1'b0}}, input_multiplier};  // Bit_Extender bit_extender_2
  assign bit_extender_3_out = {{4{1'b0}}, input_mutiplicand};  // Bit_Extender bit_extender_3
  fsm fsm_1 (.input1(bit_extender_1_out), .input0(bit_extender_2_out), .rest_bit(reset), .output0(fsm_1_output0));
  fsm fsm_2 (.input1(shifter_2_out), .input0(bit_extender_3_out), .rest_bit(reset), .output0(fsm_2_output0));
  Bit_Extender #(.out_width(4), .\type ("zero")) bit_extender_4 (.in(fsm_1_output0), .out(bit_extender_4_out));
  Register #(.width(4)) register_1 (
    .D(bit_extender_4_out), .clk(clock_1_out), .Q(register_1_q), .clr(reset));  // open: en
  Clock clock_1 (.out(clock_1_out));
  Register multiplicand (.D(fsm_2_output0), .clk(clock_2_out), .Q(multiplicand_q), .clr(reset));  // open: en
  Clock clock_2 (.out(clock_2_out));
  Shifter #(.shift("lr"), .width(4)) shifter_1 (.in(register_1_q), .\dist (2'b01), .out(shifter_1_out));
  Bit_Extender #(.in_width(4), .out_width(1), .\type ("zero")) bit_extender_5 (
    .in(register_1_q), .out(bit_extender_5_out));
  Shifter shifter_2 (.in(multiplicand_q), .\dist (3'b001), .out(shifter_2_out));
  // Probe on shifter_1_out
  Adder adder_1 (.a(out_4), .b(multiplicand_q), .out(adder_1_out));  // open: cin, cout
  Multiplexer #(.enable("false"), .width(8)) multiplexer_1 (
    .in0(out_4), .in1(adder_1_out), .out(multiplexer_1_out), .sel(bit_extender_5_out));
  Register product (.D(multiplexer_1_out), .clk(clock_3_out), .Q(out_4), .clr(reset));  // open: en
  Clock clock_3 (.out(clock_3_out));
endmodule

module fsm (
  input  [7:0] input1,
  input  [7:0] input0,
  input  rest_bit,
  output [7:0] output0
);

  wire clock_1_out, fsm_logic_1_next_state, fsm_logic_1_output_bit, not_1_out, register_1_q;

  not not_1 (not_1_out, rest_bit);
  Multiplexer #(.enable("false"), .width(8)) multiplexer_1 (
    .in0(input0), .in1(input1), .out(output0), .sel(fsm_logic_1_output_bit));
  fsm_logic fsm_logic_1 (
    .input_bit(not_1_out), .current_state(register_1_q), .next_state(fsm_logic_1_next_state),
    .output_bit(fsm_logic_1_output_bit));
  Clock clock_1 (.out(clock_1_out));
  Register #(.width(1)) register_1 (
    .D(fsm_logic_1_next_state), .clk(clock_1_out), .Q(register_1_q), .clr(rest_bit));  // open: en
endmodule

module fsm_logic (
  input  input_bit,
  input  current_state,
  output next_state,
  output output_bit
);

  and and_1 (output_bit, input_bit, current_state);

  assign next_state = input_bit;
endmodule
