// Logisim project pipelining_curcit.circ as structural Verilog: 1 circuit, main circuit main
module main (
);

  wire clk;
  wire [7:0] adder_1_out, adder_2_out, adder_3_out, register_1_q, register_2_q, register_3_q;

  Clock clock_1 (.out(clk));
  Adder adder_1 (.a(8'h1), .b(register_1_q), .out(adder_1_out));  // open: cin, cout
  // Probe on adder_1_out
  Register register_1 (.D(adder_1_out), .clk(clk), .Q(register_1_q));  // open: en, clr
  Adder adder_2 (.a(adder_1_out), .b(adder_1_out), .out(adder_2_out));  // open: cin, cout
  // Probe on adder_2_out
  Register register_2 (.D(adder_2_out), .clk(clk), .Q(register_2_q));  // open: en, clr
  Register register_3 (.D(adder_3_out), .clk(clk), .Q(register_3_q));  // open: en, clr
  Adder adder_3 (.a(register_2_q), .b(8'h1), .out(adder_3_out));  // open: cin, cout
  // Probe on register_3_q
endmodule
